// Digital circuit basys_clock.dig as structural Verilog
module basys_clock (
  input  Clock,
  input  Clock_2,
  input  Center,
  input  SW0,
  input  SW1,
  input  SW2,
  input  SW3,
  input  SW4,
  input  SW5,
  input  SW6,
  input  SW8,
  input  SW9,
  input  SW10,
  input  SW12,
  input  SW13,
  output AN3,
  output AN2,
  output AN1,
  output AN0,
  output CD,
  output CC,
  output CB,
  output CA,
  output CE,
  output CF,
  output CG,
  output DP,
  output JB1,
  output JB2,
  output JB3,
  output JB4,
  output JB7,
  output JB8,
  output JB9,
  output JB10
);

  wire and_1_out, d_ff_1_nq, d_ff_1_q, multiplexer_1_out, multiplexer_2_out, multiplexer_4_out,
       multiplexer_7_out, scuffed_delay_1_out, scuffed_delay_2_out, scuffed_delay_3_out, scuffed_delay_4_out,
       scuffed_delay_5_out, seven_seg_cmpl_1_an_0, seven_seg_cmpl_1_an_1, seven_seg_cmpl_1_an_2,
       seven_seg_cmpl_1_an_3;
  wire [3:0] d_ff_3_q, d_ff_4_q, d_ff_5_q, d_ff_6_q, incr_4bit_1_out, incr_4bit_2_out, incr_4bit_3_out,
       incr_4bit_4_out, multiplexer_3_out, multiplexer_5_out, multiplexer_6_out, multiplexer_8_out, or_2_out,
       or_3_out, or_4_out, or_5_out;
  wire [3:3] comp_4bit_4_out;
  wire [5:0] d_ff_2_q, incr_6bit_1_out, or_1_out;

  D_FF d_ff_1 (.D(d_ff_1_nq), .C(Center), .Q(d_ff_1_q), .nQ(d_ff_1_nq));
  and and_1 (and_1_out, Clock_2, d_ff_1_q);
  incr_6bit incr_6bit_1 (.IN(or_1_out), .EN(and_1_out), .OUT(incr_6bit_1_out));
  scuffed_delay scuffed_delay_1 (.IN(and_1_out), .OUT(scuffed_delay_1_out));
  comp_6bit comp_6bit_1 (.B(d_ff_2_q), .A(6'b111011), .OUT(JB1));
  assign or_1_out = d_ff_2_q | {6{JB1}};  // Or or_1, 6 bits wide
  D_FF #(.Bits(6)) d_ff_2 (.D(incr_6bit_1_out), .C(scuffed_delay_1_out), .Q(d_ff_2_q));  // open: nQ
  incr_4bit incr_4bit_1 (.IN(or_2_out), .EN(JB1), .OUT(incr_4bit_1_out));
  Multiplexer multiplexer_1 (.sel(Center), .in_0(JB1), .in_1(Center), .out(multiplexer_1_out));
  comp_4bit comp_4bit_1 (.B(multiplexer_3_out), .A(4'b1010), .OUT(JB7));
  scuffed_delay scuffed_delay_2 (.IN(multiplexer_1_out), .OUT(scuffed_delay_2_out));
  assign or_2_out = multiplexer_3_out | {4{JB7}};  // Or or_2, 4 bits wide
  D_FF #(.Bits(4)) d_ff_3 (.D(incr_4bit_1_out), .C(scuffed_delay_2_out), .Q(d_ff_3_q));  // open: nQ
  incr_4bit incr_4bit_2 (.IN(or_3_out), .EN(JB7), .OUT(incr_4bit_2_out));
  Multiplexer multiplexer_2 (.sel(Center), .in_0(JB7), .in_1(Center), .out(multiplexer_2_out));
  Multiplexer #(.Bits(4)) multiplexer_3 (
    .sel(Center), .in_0(d_ff_3_q), .in_1({SW3, SW2, SW1, SW0}), .out(multiplexer_3_out));
  comp_4bit comp_4bit_2 (.B(multiplexer_5_out), .A(4'b0110), .OUT(JB2));
  assign or_3_out = multiplexer_5_out | {4{JB2}};  // Or or_3, 4 bits wide
  scuffed_delay scuffed_delay_3 (.IN(multiplexer_2_out), .OUT(scuffed_delay_3_out));
  D_FF #(.Bits(4)) d_ff_4 (.D(incr_4bit_2_out), .C(scuffed_delay_3_out), .Q(d_ff_4_q));  // open: nQ
  incr_4bit incr_4bit_3 (.IN(or_4_out), .EN(JB2), .OUT(incr_4bit_3_out));
  Multiplexer multiplexer_4 (.sel(Center), .in_0(JB2), .in_1(Center), .out(multiplexer_4_out));
  Multiplexer #(.Bits(4)) multiplexer_5 (
    .sel(Center), .in_0(d_ff_4_q), .in_1({1'b0, SW6, SW5, SW4}), .out(multiplexer_5_out));
  comp_4bit comp_4bit_3 (.B(multiplexer_6_out), .A(4'b0110), .OUT(JB8));
  scuffed_delay scuffed_delay_4 (.IN(multiplexer_4_out), .OUT(scuffed_delay_4_out));
  assign or_4_out = multiplexer_6_out | {4{JB8}};  // Or or_4, 4 bits wide
  D_FF #(.Bits(4)) d_ff_5 (.D(incr_4bit_3_out), .C(scuffed_delay_4_out), .Q(d_ff_5_q));  // open: nQ
  Multiplexer #(.Bits(4)) multiplexer_6 (
    .sel(Center), .in_0(d_ff_5_q), .in_1({1'b0, SW10, SW9, SW8}), .out(multiplexer_6_out));
  incr_4bit incr_4bit_4 (.IN(or_5_out), .EN(JB8), .OUT(incr_4bit_4_out));
  Multiplexer multiplexer_7 (.sel(Center), .in_0(JB8), .in_1(Center), .out(multiplexer_7_out));
  comp_4bit comp_4bit_4 (.B(multiplexer_8_out), .A(4'b0100), .OUT(comp_4bit_4_out[3]));
  assign or_5_out = multiplexer_8_out | {4{comp_4bit_4_out[3]}};  // Or or_5, 4 bits wide
  scuffed_delay scuffed_delay_5 (.IN(multiplexer_7_out), .OUT(scuffed_delay_5_out));
  D_FF #(.Bits(4)) d_ff_6 (.D(incr_4bit_4_out), .C(scuffed_delay_5_out), .Q(d_ff_6_q));  // open: nQ
  Multiplexer #(.Bits(4)) multiplexer_8 (
    .sel(Center), .in_0(d_ff_6_q), .in_1({2'b00, SW13, SW12}), .out(multiplexer_8_out));
  seven_seg_cmpl seven_seg_cmpl_1 (
    .SEG_3(multiplexer_8_out), .SEG_2(multiplexer_6_out), .SEG_1(multiplexer_5_out),
    .SEG_0(multiplexer_3_out), .CLK(Clock), .a(CA), .b(CB), .c(CC), .d(CD), .e(CE), .f(CF), .g(CG),
    .AN_3(seven_seg_cmpl_1_an_3), .AN_2(seven_seg_cmpl_1_an_2), .AN_1(seven_seg_cmpl_1_an_1),
    .AN_0(seven_seg_cmpl_1_an_0));
  not not_1 (AN0, seven_seg_cmpl_1_an_0);
  not not_2 (AN1, seven_seg_cmpl_1_an_1);
  not not_3 (AN2, seven_seg_cmpl_1_an_2);
  not not_4 (AN3, seven_seg_cmpl_1_an_3);

  assign DP = 1'b0;
  assign JB3 = Center;
  assign JB4 = JB2;
  assign JB9 = JB7;
  assign JB10 = JB8;

  // Notes on the sheet:
  //   AN3: pin W4
  //   AN2: pin V4
  //   AN1: pin U4
  //   AN0: pin U2
  //   CD: pin V8
  //   CC: pin U8
  //   CB: pin W6
  //   CA: pin W7
  //   CE: pin U5
  //   CF: pin V5
  //   CG: pin U7
  //   DP: pin V7
  //   Clock: pin W5, Hz: 200
  //   Clock_2: pin W5, Hz: 10
  //   Center: pin U18
  //   SW0: pin V17
  //   SW1: pin V16
  //   SW2: pin W16
  //   SW3: pin W17
  //   SW4: pin W15
  //   SW5: pin V15
  //   SW6: pin W14
  //   SW8: pin V2
  //   SW9: pin T3
  //   SW10: pin T2
  //   SW12: pin W2
  //   SW13: pin U1
  //   JB1: pin A14
  //   JB2: pin A16
  //   JB3: pin B15
  //   JB4: pin B16
  //   JB7: pin A15
  //   JB8: pin A17
  //   JB9: pin C15
  //   JB10: pin C16
endmodule
