// Digital circuit comp_4bit.dig as structural Verilog
module comp_4bit (
  input  [3:0] B,
  input  [3:0] A,
  output OUT
);

  wire [3:0] xnor_1_out;

  assign xnor_1_out = ~(B ^ A);  // XNOr xnor_1, 4 bits wide
  and and_1 (OUT, xnor_1_out[0], xnor_1_out[1], xnor_1_out[2], xnor_1_out[3]);
  // Pins of 1 and 4 bits meet at A
endmodule
