// Digital circuit comp_6bit.dig as structural Verilog
module comp_6bit (
  input  [5:0] B,
  input  [5:0] A,
  output OUT
);

  wire [5:0] xnor_1_out;

  assign xnor_1_out = ~(B ^ A);  // XNOr xnor_1, 6 bits wide
  and and_1 (OUT, xnor_1_out[0], xnor_1_out[1], xnor_1_out[2], xnor_1_out[3], xnor_1_out[4], xnor_1_out[5]);
endmodule
