// Digital circuit incr_4bit.dig as structural Verilog
module incr_4bit (
  input  [3:0] IN,
  input  EN,
  output [3:0] OUT
);

  wire halfadder_2_c, halfadder_3_c, halfadder_4_c;

  halfAdder halfadder_1 (.A(IN[3]), .B(halfadder_2_c), .S(OUT[3]));  // open: C
  halfAdder halfadder_2 (.A(IN[2]), .B(halfadder_3_c), .S(OUT[2]), .C(halfadder_2_c));
  halfAdder halfadder_3 (.A(IN[1]), .B(halfadder_4_c), .S(OUT[1]), .C(halfadder_3_c));
  halfAdder halfadder_4 (.A(IN[0]), .B(EN), .S(OUT[0]), .C(halfadder_4_c));
endmodule
