// Digital circuit incr_6bit.dig as structural Verilog
module incr_6bit (
  input  [5:0] IN,
  input  EN,
  output [5:0] OUT
);

  wire halfadder_2_c, halfadder_3_c, halfadder_4_c, halfadder_5_c, halfadder_6_c;

  halfAdder halfadder_1 (.A(IN[5]), .B(halfadder_2_c), .S(OUT[5]));  // open: C
  halfAdder halfadder_2 (.A(IN[4]), .B(halfadder_3_c), .S(OUT[4]), .C(halfadder_2_c));
  halfAdder halfadder_3 (.A(IN[3]), .B(halfadder_4_c), .S(OUT[3]), .C(halfadder_3_c));
  halfAdder halfadder_4 (.A(IN[2]), .B(halfadder_5_c), .S(OUT[2]), .C(halfadder_4_c));
  halfAdder halfadder_5 (.A(IN[1]), .B(halfadder_6_c), .S(OUT[1]), .C(halfadder_5_c));
  halfAdder halfadder_6 (.A(IN[0]), .B(EN), .S(OUT[0]), .C(halfadder_6_c));
endmodule
